// Logisim project RISCVMicroprocessor.circ as structural Verilog: 8 circuits, main circuit main
module main (
  input  in_1,
  input  in_2,
  output [4:0] out_3
);

  wire and_1_out, clock_1_out, control_unit_1_auipc_2, control_unit_1_branch, control_unit_1_jal_2,
       control_unit_1_jalr_2, control_unit_1_lui_2, control_unit_1_memread, control_unit_1_memwrite,
       control_unit_1_operand_b_selext, control_unit_1_regwrite, multiplexer_7_out, or_1_out, type_1_auipc,
       type_1_i_type, type_1_jal, type_1_jalr, type_1_load, type_1_lui, type_1_r_type, type_1_s_type;
  wire [4:0] multiplexer_6_out, rom_1_data_2;
  wire [6:0] rom_1_data;
  wire [31:0] adder_1_out, adder_2_out, adder_3_out, adder_4_out, alu_1_output, Immediate_Generator_i_type,
       Immediate_Generator_s_type, Immediate_Generator_sb_type, Immediate_Generator_u_type,
       Immediate_Generator_uj_type, multiplexer_1_out, multiplexer_2_out, multiplexer_3_out,
       multiplexer_5_out, multiplexer_8_out, multiplexer_9_out, multiplexer_10_out, multiplexer_11_out,
       multiplexer_12_out, ram_1_data, register_1_q, register_file_1_read_data1, register_file_1_read_data_2,
       shifter_1_out;
  wire [31:15] rom_1_data_3;

  Multiplexer #(.width(32), .disabled(0), .enable("false")) multiplexer_1 (
    .in0(multiplexer_2_out), .in1(alu_1_output), .out(multiplexer_1_out), .sel(control_unit_1_jalr_2));
  Multiplexer #(.width(32), .disabled(0), .enable("false")) multiplexer_2 (
    .in0(adder_1_out), .in1(adder_2_out), .out(multiplexer_2_out), .sel(or_1_out));
  Register #(.width(32)) register_1 (.D(multiplexer_3_out), .Q(register_1_q), .clk(clock_1_out));  // open: en, clr
  Multiplexer #(.width(32), .enable("false")) multiplexer_3 (
    .in0(multiplexer_1_out), .in1(adder_4_out), .out(multiplexer_3_out), .sel(and_1_out));
  Clock clock_1 (.out(clock_1_out));
  Adder #(.width(32)) adder_1 (.a(32'h4), .b(register_1_q), .out(adder_1_out));  // open: cin, cout
  ROM #(.addrWidth(24), .dataWidth(32)) rom_1 (
    .addr(register_1_q[25:2]), .data({rom_1_data_3, out_3[2:0], rom_1_data_2, rom_1_data}));  // open: sel
  \type  type_1 (
    .in_1(rom_1_data), .R_type(type_1_r_type), .I_type(type_1_i_type), .s_type(type_1_s_type),
    .LUI(type_1_lui), .SB_type(out_3[4]), .JAL(type_1_jal), .LOAD(type_1_load), .AUIPC(type_1_auipc),
    .JALR(type_1_jalr));
  circuit Immediate_Generator (
    .in_1({rom_1_data_3, out_3[2:0], rom_1_data_2, rom_1_data}), .I_TYPE(Immediate_Generator_i_type),
    .S_TYPE(Immediate_Generator_s_type), .SB_TYPE(Immediate_Generator_sb_type),
    .U_TYPE(Immediate_Generator_u_type), .UJ_TYPE(Immediate_Generator_uj_type));
  Multiplexer #(.enable("false")) multiplexer_4 (.in0(rom_1_data_3[30]), .in1(1'b0), .out(out_3[3]), .sel(out_3[4]));
  Multiplexer #(.width(32), .enable("false")) multiplexer_5 (
    .in0(Immediate_Generator_i_type), .in1(Immediate_Generator_s_type), .out(multiplexer_5_out),
    .sel(multiplexer_7_out));
  Control_Unit control_unit_1 (
    .MEMWRITE(control_unit_1_memwrite), .BRANCH(control_unit_1_branch), .MEMREAD(control_unit_1_memread),
    .REGWRITE(control_unit_1_regwrite), .MEMTOREG(control_unit_1_memread),
    .Operand_B_Selext(control_unit_1_operand_b_selext), .JALR_2(control_unit_1_jalr_2),
    .JAL_2(control_unit_1_jal_2), .LUI_2(control_unit_1_lui_2), .AUIPC_2(control_unit_1_auipc_2),
    .R(type_1_r_type), .Load(type_1_load), .jalr(type_1_jalr), .I(type_1_i_type), .store(type_1_s_type),
    .AUIPC(type_1_auipc), .LUI(type_1_lui), .SB(out_3[4]), .JAL(type_1_jal));
  Shifter #(.width(32)) shifter_1 (.in(Immediate_Generator_u_type), .\dist (5'b10010), .out(shifter_1_out));
  Adder #(.width(32)) adder_2 (
    .a(Immediate_Generator_uj_type), .b(register_1_q), .out(adder_2_out));  // open: cin, cout
  Adder #(.width(32)) adder_3 (.a(shifter_1_out), .b(register_1_q), .out(adder_3_out));  // open: cin, cout
  Multiplexer #(.width(5), .enable("false")) multiplexer_6 (
    .in0(rom_1_data_2), .in1(5'b00001), .out(multiplexer_6_out), .sel(or_1_out));
  Multiplexer #(.enable("false")) multiplexer_7 (
    .in0(type_1_i_type), .in1(type_1_s_type), .out(multiplexer_7_out), .sel(type_1_s_type));
  Adder #(.width(32)) adder_4 (
    .a(Immediate_Generator_sb_type), .b(register_1_q), .out(adder_4_out));  // open: cin, cout
  Multiplexer #(.width(32), .enable("false")) multiplexer_8 (
    .in0(multiplexer_12_out), .in1(adder_1_out), .out(multiplexer_8_out), .sel(or_1_out));
  Register_file register_file_1 (
    .rd(multiplexer_6_out), .Write_en(control_unit_1_regwrite), .read_data1(register_file_1_read_data1),
    .rs1(rom_1_data_3[19:15]), .read_data_2(register_file_1_read_data_2), .rs2(rom_1_data_3[24:20]),
    .write_data(multiplexer_10_out), .in_6(clock_1_out));
  Multiplexer #(.width(32), .enable("false")) multiplexer_9 (
    .in0(multiplexer_8_out), .in1(adder_3_out), .out(multiplexer_9_out), .sel(control_unit_1_auipc_2));
  Multiplexer #(.width(32), .enable("false")) multiplexer_10 (
    .in0(multiplexer_9_out), .in1(shifter_1_out), .out(multiplexer_10_out), .sel(control_unit_1_lui_2));
  Multiplexer #(.width(32), .enable("false")) multiplexer_11 (
    .in0(register_file_1_read_data_2), .in1(multiplexer_5_out), .out(multiplexer_11_out),
    .sel(control_unit_1_operand_b_selext));
  or or_1 (or_1_out, control_unit_1_jalr_2, control_unit_1_jal_2);
  Multiplexer #(.width(32), .enable("false")) multiplexer_12 (
    .in0(alu_1_output), .in1(ram_1_data), .out(multiplexer_12_out), .sel(control_unit_1_memread));
  ALU alu_1 (.OUTPUT(alu_1_output), .rs1(register_file_1_read_data1), .rs2(multiplexer_11_out), .fun3_fuc7(out_3));
  and and_1 (and_1_out, control_unit_1_branch, alu_1_output[0]);
  RAM #(.addrWidth(24), .dataWidth(32), .bus("separate")) ram_1 (
    .addr(alu_1_output[24:1]), .din(multiplexer_11_out), .data(ram_1_data), .str(control_unit_1_memwrite),
    .sel(in_1), .clk(in_2), .ld(control_unit_1_memread));  // open: clr

  // Notes on the sheet:
  //   jal
  //   jalr
  //   JAL SELECT
  //   sb
  //   PC
  //   CLOCK
  //   TYPE IDENTIFER
  //   I-type
  //   s-type
  //   RV 32I SINGLE CYCLE PROCESSOR
  //   PC+{IMM,1B'0}
  //   JAL
  //   I/S OPCODE 
  //   AUIPC
  //   SB
  //   PC+4
  //   AUIPC
  //   LUI
  //   SB
endmodule

module \type  (
  input  [6:0] in_1,
  output R_type,
  output LOAD,
  output I_type,
  output JALR,
  output s_type,
  output AUIPC,
  output LUI,
  output SB_type,
  output JAL
);

  Comparator #(.width(7)) comparator_1 (.a(7'b0110011), .b(in_1), .eq(R_type));  // open: gt, lt
  Comparator #(.width(7)) comparator_2 (.a(7'b0000011), .b(in_1), .eq(LOAD));  // open: gt, lt
  Comparator #(.width(7)) comparator_3 (.a(7'b0010011), .b(in_1), .eq(I_type));  // open: gt, lt
  Comparator #(.width(7)) comparator_4 (.a(7'b1100111), .b(in_1), .eq(JALR));  // open: gt, lt
  Comparator #(.width(7)) comparator_5 (.a(7'b0100011), .b(in_1), .eq(s_type));  // open: gt, lt
  Comparator #(.width(7)) comparator_6 (.a(7'b0010111), .b(in_1), .eq(AUIPC));  // open: gt, lt
  Comparator #(.width(7)) comparator_7 (.a(7'b0110111), .b(in_1), .eq(LUI));  // open: gt, lt
  Comparator #(.width(7)) comparator_8 (.a(7'b1100011), .b(in_1), .eq(SB_type));  // open: gt, lt
  Comparator #(.width(7)) comparator_9 (.a(7'b1101111), .b(in_1), .eq(JAL));  // open: gt, lt

  // Notes on the sheet:
  //   R-type
  //   I-type
  //   s-type
  //   U-type
  //   SB-type
  //   UJ-type
endmodule

module circuit (
  input  [31:0] in_1,
  output [31:0] I_TYPE,
  output [31:0] S_TYPE,
  output [31:0] SB_TYPE,
  output [31:0] U_TYPE,
  output [31:0] UJ_TYPE
);

  assign I_TYPE = {{20{in_1[31]}}, in_1[31:20]};  // Bit_Extender bit_extender_1
  assign S_TYPE = {{20{in_1[31]}}, {in_1[31:25], in_1[11:7]}};  // Bit_Extender bit_extender_2
  assign SB_TYPE = {{19{in_1[31]}}, {in_1[31], in_1[7], in_1[30:25], in_1[11:8], 1'b0}};  // Bit_Extender bit_extender_3
  assign U_TYPE = {{12{in_1[31]}}, in_1[31:12]};  // Bit_Extender bit_extender_4
  assign UJ_TYPE = {{11{in_1[31]}}, {in_1[31], in_1[19:12], in_1[20], in_1[30:21], 1'b0}};  // Bit_Extender bit_extender_5

  // Notes on the sheet:
  //   I-type
  //   S-type
  //   SB-type
  //   U-type
  //   UJ-type
endmodule

module Alu_controller (
  input  [31:0] in_1
);
endmodule

module ALU (
  input  [31:0] rs1,
  input  [31:0] rs2,
  input  [4:0] fun3_fuc7,
  output [31:0] OUTPUT
);

  wire adder_2_cout, comparator_1_lt, comparator_2_lt, comparator_3_eq, comparator_4_eq, comparator_5_eq,
       comparator_5_gt, comparator_6_eq, comparator_6_gt, not_2_out, or_2_out, or_3_out;
  wire [31:0] adder_1_out, adder_2_out, AND_out, multiplexer_1_out, multiplexer_3_out, multiplexer_4_out,
       multiplexer_5_out, multiplexer_6_out, multiplexer_7_out, multiplexer_8_out, not_1_out, OR_out,
       shifter_1_out, shifter_2_out, shifter_3_out, xor_1_out;

  Adder #(.width(32)) adder_1 (.a(rs2), .b(rs1), .out(adder_1_out));  // open: cin, cout
  LED led_1 (.in(adder_2_cout));
  Multiplexer #(.width(32), .enable("false")) multiplexer_1 (
    .in0(rs2), .in1(not_1_out), .out(multiplexer_1_out), .sel(1'b1));
  Adder #(.width(32)) adder_2 (.a(multiplexer_1_out), .b(rs1), .out(adder_2_out), .cin(1'b1), .cout(adder_2_cout));
  assign not_1_out = ~rs2;  // NOT_Gate not_1, 32 bits wide
  Shifter #(.width(32)) shifter_1 (.in(rs1), .\dist (rs2[4:0]), .out(shifter_1_out));
  Multiplexer #(.select(5), .width(32), .enable("false")) multiplexer_2 (
    .in0(adder_1_out), .in1(shifter_1_out), .in2(multiplexer_3_out), .in3(multiplexer_4_out),
    .in4(xor_1_out), .in5(shifter_2_out), .in6(OR_out), .in7(AND_out), .in8(adder_2_out),
    .in13(shifter_3_out), .in16(multiplexer_5_out), .in17(multiplexer_6_out), .in20(multiplexer_3_out),
    .in21(multiplexer_7_out), .in22(multiplexer_4_out), .in23(multiplexer_8_out), .out(OUTPUT),
    .sel(fun3_fuc7));  // open: in9, in10, in11, in12, in14, in15, in18, in19, in24, in25, in26, in27, in28, in29, in30, in31
  Comparator #(.width(32)) comparator_1 (.a(rs1), .b(rs2), .lt(comparator_1_lt));  // open: gt, eq
  Multiplexer #(.width(32), .enable("false")) multiplexer_3 (
    .in0({32{1'b0}}), .in1(32'h1), .out(multiplexer_3_out), .sel(comparator_1_lt));
  Comparator #(.width(32), .mode("unsigned")) comparator_2 (.a(rs1), .b(rs2), .lt(comparator_2_lt));  // open: gt, eq
  Multiplexer #(.width(32), .enable("false")) multiplexer_4 (
    .in0({32{1'b0}}), .in1(32'h1), .out(multiplexer_4_out), .sel(comparator_2_lt));
  assign xor_1_out = rs2 ^ rs2;  // XOR_Gate xor_1, 32 bits wide
  Shifter #(.width(32), .shift("lr")) shifter_2 (.in(rs2), .\dist (rs2[4:0]), .out(shifter_2_out));
  Shifter #(.width(32), .shift("ar")) shifter_3 (.in(rs2), .\dist (rs2[4:0]), .out(shifter_3_out));
  assign OR_out = rs1 | rs2;  // OR_Gate OR, 32 bits wide
  assign AND_out = rs1 & rs2;  // AND_Gate AND, 32 bits wide
  Comparator #(.width(32)) comparator_3 (.a(rs2), .b(rs1), .eq(comparator_3_eq));  // open: gt, lt
  Multiplexer #(.width(32)) multiplexer_5 (
    .in0({32{1'b0}}), .in1(32'h1), .out(multiplexer_5_out), .sel(comparator_3_eq));  // open: en
  Comparator #(.width(32)) comparator_4 (.a(rs2), .b(rs1), .eq(comparator_4_eq));  // open: gt, lt
  not not_2 (not_2_out, comparator_4_eq);
  Multiplexer #(.width(32)) multiplexer_6 (
    .in0({32{1'b0}}), .in1(32'h1), .out(multiplexer_6_out), .sel(not_2_out));  // open: en
  Comparator #(.width(32)) comparator_5 (.a(rs2), .b(rs1), .gt(comparator_5_gt), .eq(comparator_5_eq));  // open: lt
  or or_2 (or_2_out, comparator_5_gt, comparator_5_eq);
  Multiplexer #(.width(32), .enable("false")) multiplexer_7 (
    .in0({32{1'b0}}), .in1(32'h1), .out(multiplexer_7_out), .sel(or_2_out));
  Comparator #(.width(32), .mode("unsigned")) comparator_6 (
    .a(rs2), .b(rs1), .gt(comparator_6_gt), .eq(comparator_6_eq));  // open: lt
  or or_3 (or_3_out, comparator_6_gt, comparator_6_eq);
  Multiplexer #(.width(32), .enable("false")) multiplexer_8 (
    .in0({32{1'b0}}), .in1(32'h1), .out(multiplexer_8_out), .sel(or_3_out));

  // Notes on the sheet:
  //   ADD
  //   00000----->add
  //   01000--->subtract
  //   00001-----> sll
  //   00010-----> slt
  //   00011---> sltu
  //   00100-----> xor
  //   00101---->srl
  //   01101----> sra
  //   00110---->or
  //   00111-----> and
  //   SUBTRACT
  //   SLL
  //   SLT
  //   SLTU
  //   SRL
  //   SRA
  //   BEQ
  //   BNE
endmodule

module Register_file (
  input  [4:0] rs1,
  input  [31:0] write_data,
  input  [4:0] rd,
  input  [4:0] rs2,
  input  Write_en,
  input  in_6,
  output [31:0] read_data1,
  output [31:0] read_data_2
);

  wire and_1_out, and_2_out, and_3_out, and_4_out, and_5_out, and_6_out, and_7_out, and_8_out, and_9_out,
       and_10_out, and_11_out, and_12_out, and_13_out, and_14_out, and_15_out, and_16_out, and_17_out,
       and_18_out, and_19_out, and_20_out, and_21_out, and_22_out, and_23_out, and_24_out, and_25_out,
       and_26_out, and_27_out, and_28_out, and_29_out, and_30_out, and_31_out, and_32_out, decoder_1_out0,
       decoder_1_out1, decoder_1_out2, decoder_1_out3, decoder_1_out4, decoder_1_out5, decoder_1_out6,
       decoder_1_out7, decoder_1_out8, decoder_1_out9, decoder_1_out10, decoder_1_out11, decoder_1_out12,
       decoder_1_out13, decoder_1_out14, decoder_1_out15, decoder_1_out16, decoder_1_out17, decoder_1_out18,
       decoder_1_out19, decoder_1_out20, decoder_1_out21, decoder_1_out22, decoder_1_out23, decoder_1_out24,
       decoder_1_out25, decoder_1_out26, decoder_1_out27, decoder_1_out28, decoder_1_out29, decoder_1_out30,
       decoder_1_out31, undriven;
  wire [31:0] register_1_q, register_2_q, register_3_q, register_4_q, register_5_q, register_6_q,
       register_7_q, register_8_q, register_9_q, register_10_q, register_11_q, register_12_q, register_13_q,
       register_14_q, register_15_q, register_16_q, register_17_q, register_18_q, register_19_q,
       register_20_q, register_21_q, register_22_q, register_23_q, register_24_q, register_25_q,
       register_26_q, register_27_q, register_28_q, register_29_q, register_30_q, register_31_q,
       register_32_q;

  Decoder #(.select(5), .enable("false")) decoder_1 (
    .out0(decoder_1_out0), .out1(decoder_1_out1), .out2(decoder_1_out2), .out3(decoder_1_out3),
    .out4(decoder_1_out4), .out5(decoder_1_out5), .out6(decoder_1_out6), .out7(decoder_1_out7),
    .out8(decoder_1_out8), .out9(decoder_1_out9), .out10(decoder_1_out10), .out11(decoder_1_out11),
    .out12(decoder_1_out12), .out13(decoder_1_out13), .out14(decoder_1_out14), .out15(decoder_1_out15),
    .out16(decoder_1_out16), .out17(decoder_1_out17), .out18(decoder_1_out18), .out19(decoder_1_out19),
    .out20(decoder_1_out20), .out21(decoder_1_out21), .out22(decoder_1_out22), .out23(decoder_1_out23),
    .out24(decoder_1_out24), .out25(decoder_1_out25), .out26(decoder_1_out26), .out27(decoder_1_out27),
    .out28(decoder_1_out28), .out29(decoder_1_out29), .out30(decoder_1_out30), .out31(decoder_1_out31),
    .sel(rd));
  and and_1 (and_1_out, decoder_1_out0, Write_en);
  and and_2 (and_2_out, decoder_1_out1, Write_en);
  and and_3 (and_3_out, decoder_1_out2, Write_en);
  and and_4 (and_4_out, decoder_1_out3, Write_en);
  and and_5 (and_5_out, decoder_1_out4, Write_en);
  and and_6 (and_6_out, decoder_1_out5, Write_en);
  and and_7 (and_7_out, decoder_1_out6, Write_en);
  and and_8 (and_8_out, decoder_1_out7, Write_en);
  and and_9 (and_9_out, decoder_1_out8, Write_en);
  and and_10 (and_10_out, decoder_1_out9, Write_en);
  and and_11 (and_11_out, decoder_1_out10, Write_en);
  and and_12 (and_12_out, decoder_1_out11, Write_en);
  and and_13 (and_13_out, decoder_1_out12, Write_en);
  and and_14 (and_14_out, decoder_1_out13, Write_en);
  and and_15 (and_15_out, decoder_1_out14, Write_en);
  and and_16 (and_16_out, decoder_1_out15, Write_en);
  and and_17 (and_17_out, decoder_1_out16, Write_en);
  and and_18 (and_18_out, decoder_1_out17, Write_en);
  and and_19 (and_19_out, decoder_1_out18, Write_en);
  and and_20 (and_20_out, decoder_1_out19, Write_en);
  and and_21 (and_21_out, decoder_1_out20, Write_en);
  and and_22 (and_22_out, decoder_1_out21, Write_en);
  and and_23 (and_23_out, decoder_1_out22, Write_en);
  and and_24 (and_24_out, decoder_1_out23, Write_en);
  and and_25 (and_25_out, decoder_1_out24, Write_en);
  and and_26 (and_26_out, decoder_1_out25, Write_en);
  and and_27 (and_27_out, decoder_1_out26, Write_en);
  and and_28 (and_28_out, decoder_1_out27, Write_en);
  and and_29 (and_29_out, decoder_1_out28, Write_en);
  and and_30 (and_30_out, decoder_1_out29, Write_en);
  and and_31 (and_31_out, decoder_1_out30, Write_en);
  and and_32 (and_32_out, decoder_1_out31, Write_en);
  Register #(.width(32)) register_1 (.D({32{1'b0}}), .en(and_1_out), .Q(register_1_q), .clk(in_6));  // open: clr
  Register #(.width(32)) register_2 (.D(write_data), .en(and_2_out), .Q(register_2_q), .clk(in_6));  // open: clr
  Register #(.width(32)) register_3 (.D(write_data), .en(and_3_out), .Q(register_3_q), .clk(in_6));  // open: clr
  Register #(.width(32)) register_4 (.D(write_data), .en(and_4_out), .Q(register_4_q), .clk(in_6));  // open: clr
  Register #(.width(32)) register_5 (.D(write_data), .en(and_5_out), .Q(register_5_q), .clk(in_6), .clr(undriven));
  Register #(.width(32)) register_6 (.D(write_data), .en(and_6_out), .Q(register_6_q), .clk(in_6));  // open: clr
  Register #(.width(32)) register_7 (.D(write_data), .en(and_7_out), .Q(register_7_q), .clk(in_6));  // open: clr
  Register #(.width(32)) register_8 (.D(write_data), .en(and_8_out), .Q(register_8_q), .clk(in_6));  // open: clr
  Register #(.width(32)) register_9 (.D(write_data), .en(and_9_out), .Q(register_9_q), .clk(in_6));  // open: clr
  Register #(.width(32)) register_10 (.D(write_data), .en(and_10_out), .Q(register_10_q), .clk(in_6));  // open: clr
  Register #(.width(32)) register_11 (.D(write_data), .en(and_11_out), .Q(register_11_q), .clk(in_6));  // open: clr
  Register #(.width(32)) register_12 (.D(write_data), .en(and_12_out), .Q(register_12_q), .clk(in_6));  // open: clr
  Register #(.width(32)) register_13 (.D(write_data), .en(and_13_out), .Q(register_13_q), .clk(in_6));  // open: clr
  Register #(.width(32)) register_14 (.D(write_data), .en(and_14_out), .Q(register_14_q), .clk(in_6));  // open: clr
  Register #(.width(32)) register_15 (.D(write_data), .en(and_15_out), .Q(register_15_q), .clk(in_6));  // open: clr
  Register #(.width(32)) register_16 (.D(write_data), .Q(register_16_q), .clk(in_6), .clr(and_16_out));  // open: en
  Register #(.width(32)) register_17 (.D(write_data), .en(and_17_out), .Q(register_17_q), .clk(in_6));  // open: clr
  Register #(.width(32)) register_18 (.D(write_data), .en(and_18_out), .Q(register_18_q), .clk(in_6));  // open: clr
  Register #(.width(32)) register_19 (.D(write_data), .en(and_19_out), .Q(register_19_q), .clk(in_6));  // open: clr
  Register #(.width(32)) register_20 (.D(write_data), .en(and_20_out), .Q(register_20_q), .clk(in_6));  // open: clr
  Register #(.width(32)) register_21 (.D(write_data), .en(and_21_out), .Q(register_21_q), .clk(in_6));  // open: clr
  Register #(.width(32)) register_22 (.D(write_data), .en(and_22_out), .Q(register_22_q), .clk(in_6));  // open: clr
  Register #(.width(32)) register_23 (.D(write_data), .en(and_23_out), .Q(register_23_q), .clk(in_6));  // open: clr
  Register #(.width(32)) register_24 (.D(write_data), .en(and_24_out), .Q(register_24_q), .clk(in_6));  // open: clr
  Register #(.width(32)) register_25 (.D(write_data), .en(and_25_out), .Q(register_25_q), .clk(in_6));  // open: clr
  Register #(.width(32)) register_26 (.D(write_data), .en(and_26_out), .Q(register_26_q), .clk(in_6));  // open: clr
  Register #(.width(32)) register_27 (.D(write_data), .en(and_27_out), .Q(register_27_q), .clk(in_6));  // open: clr
  Register #(.width(32)) register_28 (.D(write_data), .en(and_28_out), .Q(register_28_q), .clk(in_6));  // open: clr
  Register #(.width(32)) register_29 (.D(write_data), .en(and_29_out), .Q(register_29_q), .clk(in_6));  // open: clr
  Register #(.width(32)) register_30 (.D(write_data), .en(and_30_out), .Q(register_30_q), .clk(in_6));  // open: clr
  Register #(.width(32)) register_31 (.D(write_data), .en(and_31_out), .Q(register_31_q), .clk(in_6));  // open: clr
  Register #(.width(32)) register_32 (.D(write_data), .en(and_32_out), .Q(register_32_q), .clk(in_6));  // open: clr
  Multiplexer #(.select(5), .width(32), .enable("false")) multiplexer_1 (
    .in0(register_1_q), .in1(register_2_q), .in2(register_3_q), .in3(register_4_q), .in4(register_5_q),
    .in5(register_6_q), .in6(register_7_q), .in7(register_8_q), .in8(register_9_q), .in9(register_10_q),
    .in10(register_11_q), .in11(register_12_q), .in12(register_13_q), .in13(register_14_q),
    .in14(register_15_q), .in15(register_16_q), .in16(register_17_q), .in17(register_18_q),
    .in18(register_19_q), .in19(register_20_q), .in20(register_21_q), .in21(register_22_q),
    .in22(register_23_q), .in23(register_24_q), .in24(register_25_q), .in25(register_26_q),
    .in26(register_27_q), .in27(register_28_q), .in28(register_29_q), .in29(register_30_q),
    .in30(register_31_q), .in31(register_32_q), .out(read_data1), .sel(rs1));
  Multiplexer #(.select(5), .width(32), .enable("false")) multiplexer_2 (
    .in0(register_1_q), .in1(register_2_q), .in2(register_3_q), .in3(register_4_q), .in4(register_5_q),
    .in5(register_6_q), .in6(register_7_q), .in7(register_8_q), .in8(register_9_q), .in9(register_10_q),
    .in10(register_11_q), .in11(register_12_q), .in12(register_13_q), .in13(register_14_q),
    .in14(register_15_q), .in15(register_16_q), .in16(register_17_q), .in17(register_18_q),
    .in18(register_19_q), .in19(register_20_q), .in20(register_21_q), .in21(register_22_q),
    .in22(register_23_q), .in23(register_24_q), .in24(register_25_q), .in25(register_26_q),
    .in26(register_27_q), .in27(register_28_q), .in28(register_29_q), .in29(register_30_q),
    .in30(register_31_q), .in31(register_32_q), .out(read_data_2), .sel(rs2));
endmodule

// CONTROL UNIT
module Control_Unit (
  input  LUI,
  input  SB,
  input  JAL,
  input  R,
  input  Load,
  input  I,
  input  jalr,
  input  store,
  input  AUIPC,
  output MEMWRITE,
  output BRANCH,
  output MEMREAD,
  output REGWRITE,
  output MEMTOREG,
  output Operand_B_Selext,
  output JALR_2,
  output JAL_2,
  output LUI_2,
  output AUIPC_2
);

  or or_1 (REGWRITE, JAL, Load, jalr, LUI, R, I, AUIPC);
  or or_2 (Operand_B_Selext, store, Load, I);

  assign AUIPC_2 = AUIPC;
  assign BRANCH = SB;
  assign JAL_2 = JAL;
  assign JALR_2 = jalr;
  assign LUI_2 = LUI;
  assign MEMREAD = Load;
  assign MEMTOREG = Load;
  assign MEMWRITE = store;
endmodule

module ALUPPPPPP (
  input  R,
  input  L,
  input  I,
  input  I_TYPE,
  input  S,
  input  U,
  input  SB,
  output [2:0] out_8
);

  wire and_1_out, and_2_out, and_3_out, and_4_out, and_5_out, and_6_out, not_1_out, not_2_out, not_3_out,
       not_4_out, not_5_out, not_6_out, not_7_out, not_8_out, not_9_out, not_10_out, not_11_out, not_12_out;

  not not_1 (not_1_out, R);
  not not_2 (not_2_out, L);
  not not_3 (not_3_out, I);
  not not_4 (not_4_out, I_TYPE);
  not not_5 (not_5_out, R);
  not not_6 (not_6_out, L);
  not not_7 (not_7_out, S);
  not not_8 (not_8_out, U);
  not not_9 (not_9_out, R);
  not not_10 (not_10_out, I);
  not not_11 (not_11_out, S);
  not not_12 (not_12_out, SB);
  and and_1 (and_1_out, not_1_out, not_2_out);
  and and_2 (and_2_out, not_3_out, not_4_out);
  and and_3 (and_3_out, not_5_out, not_6_out);
  and and_4 (and_4_out, not_7_out, not_8_out);
  and and_5 (and_5_out, not_9_out, not_10_out);
  and and_6 (and_6_out, not_11_out, not_12_out);
  and and_7 (out_8[2], and_1_out, and_2_out);
  and and_8 (out_8[1], and_3_out, and_4_out);
  and and_9 (out_8[0], and_5_out, and_6_out);
endmodule
